# Fritzing sketch DIR-868L-A1 (saved by Fritzing 0.9.3b)
breadboards: 1

parts:
  Part1 = Arduino Uno (Rev3)
  R1 = Resistor [tolerance=±5% resistance=1k package=THT]
  R2 = Resistor [tolerance=±5% resistance=2.2k package=THT]
  R3 = Resistor [tolerance=±5% resistance=1k package=THT]
  R4 = Resistor [tolerance=±5% resistance=220 package=THT]
  TP1 = TEST-POINT [package=pad.03x.05]
  TP2 = TEST-POINT [package=pad.03x.05]
  TP3 = TEST-POINT [package=pad.03x.05]  # not connected
  JP1 = JUMPER-3-OLD [package=sj_3_paste2_3]
  LED1 = LEDs [package=led10mm]  # not connected
  LED2 = LEDs [package=led10mm]  # not connected

nets:
  N1: Part1.GND, R2.Pin_0, R4.Pin_1, TP2.1
  N2: Part1.D0/RX, R3.Pin_0
  N3: Part1.D1/TX, R1.Pin_1
  N4: R1.Pin_0, R2.Pin_1, TP1.1
  N5: R3.Pin_1, R4.Pin_0, JP1.3
